# Fritzing sketch phone-temp-hum-co2-feather (saved by Fritzing 0.9.3b)
breadboards: 1

parts:
  Part1 = Adafruit Feather 32u4 FONA [part_number="Adafruit #3027"]
  Part2 = Adafruit Adalogger FeatherWing [part_number="Adafruit #2922"]
  DHT1 = DHT22 Humidity and Temperature Sensor
  BATT1 = LiPoly Battery (1300mAh)  # not connected
  R1 = Resistor [tolerance=±5% resistance=10k package=THT]

nets:
  N1: Part1.A0, DHT1.DATA, R1.Pin_1
  GND: Part1.GND, Part2.GND, DHT1.GND
  +3V3: Part1.+3V3, Part2.+3V3, DHT1.VDD, R1.Pin_0
  N2: Part1.12, Part2.SCK
  N3: Part1.11, Part2.MOSI
  N4: Part1.10, Part2.MISO
  N5: Part1.3, Part2.SCL
  N6: Part1.2, Part2.SDA

custom parts:
  Adafruit Feather 32u4 FONA: This is the Adafruit Feather 32u4 FONA - our take on an 'all-in-one' Arduino-compatible + audio/sms/data capable cellular with built in USB and battery charging. Its an Adafruit Feather 32u4 with a FONA800 module, ready to rock! We have other boards and accessories in the Feather family, check'em out here. At the Feather 32u4's heart is at ATmega32u4 clocked at 8 MHz and at 3.3V logic, a chip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
  Adafruit Adalogger FeatherWing: This is the Adalogger FeatherWing: it adds both a battery-backed Real Time Clock and micro SD card storage to any Feather main board. This FeatherWing will make it real easy to add datalogging to any of our existing Feathers. You get both an I2C real time clock (PCF8523) with 32KHz crystal and battery backup, and a microSD socket that connects to the SPI port pins (+ extra pin for CS). Tested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
  LiPoly Battery (1300mAh): Lithium Ion Polymer Battery (1300mAh)
